// Logisim project CPU.circ as structural Verilog: 8 circuits, main circuit CPU
module CPU (
);

  wire and_1_out, and_2_out, ENABLE_ULA, JMP_X, K0, K1, K2, K3, L0, L1, L2, L3, L4, L5, L6, L7, L8, L9,
       LOAD_REG1, LOAD_REG2, or_1_out, or_2_out, RESET_PC, RESET_REG, S0, S1, S2, S3, S4, S5, S6, S7, S8, S9;
  wire [1:0] uc_1_rgin, uc_1_rgto, uc_1_ula;
  wire [3:0] HEX0, HEX1, HEX2, HEX3, HEX4, HEX5, multiplexer_1_out, TO_REG1, TO_REG2, ULA_r, X, X_forJMP;
  wire [15:0] ROM_data;

  Hex_Digit_Display hex_digit_display_1 (.value(HEX5));  // open: dp
  LED u_L9 (.in(L9));
  // DipSwitch #(.NSwitches(1)) S9: pin names not known; wires that end beside it: S9
  Hex_Digit_Display hex_digit_display_2 (.value(HEX4));  // open: dp
  LED u_L6 (.in(L6));
  LED u_L8 (.in(L8));
  LED u_L7 (.in(L7));
  // DipSwitch #(.NSwitches(1)) S8: pin names not known; wires that end beside it: S8
  // DipSwitch #(.NSwitches(1)) S6: pin names not known; wires that end beside it: S6
  // DipSwitch #(.NSwitches(1)) S7: pin names not known; wires that end beside it: S7
  or or_1 (or_1_out, S0, RESET_PC);
  Hex_Digit_Display hex_digit_display_3 (.value(HEX2));  // open: dp
  Hex_Digit_Display hex_digit_display_4 (.value(HEX3));  // open: dp
  LED u_L5 (.in(L5));
  LED u_L4 (.in(L4));
  // DipSwitch #(.NSwitches(1)) S4: pin names not known; wires that end beside it: S4
  // DipSwitch #(.NSwitches(1)) S5: pin names not known; wires that end beside it: S5
  // DipSwitch #(.NSwitches(1)) S3: pin names not known; wires that end beside it: S3
  Count8 count8_1 (
    .CLK(S9), .Vcc(1'b1), .JMP(JMP_X), .X(X_forJMP), .CLR(or_1_out), .Q({L7, L6, L5, L4, L3, L2, L1, L0}));
  Hex_Digit_Display hex_digit_display_5 (.value(HEX1));  // open: dp
  LED u_L1 (.in(L1));
  LED u_L2 (.in(L2));
  LED u_L3 (.in(L3));
  // DipSwitch #(.NSwitches(1)) S1: pin names not known; wires that end beside it: S1
  // DipSwitch #(.NSwitches(1)) S2: pin names not known; wires that end beside it: S2
  Hex_Digit_Display hex_digit_display_6 (.value(HEX0));  // open: dp
  LED u_L0 (.in(L0));
  // DipSwitch #(.NSwitches(1)) S0: pin names not known; wires that end beside it: S0
  Button u_K3 (.out(K3));
  ROM #(.dataWidth(16), .Select("low")) ROM (.addr({L7, L6, L5, L4, L3, L2, L1, L0}), .data(ROM_data));
  REG4 reg4_1 (.CLK(S9), .D(TO_REG1), .CLR(or_2_out), .Load(and_1_out), .Q(HEX1));  // open: PR
  and and_1 (and_1_out, ENABLE_ULA, LOAD_REG1);
  Button u_K0 (.out(K0));
  Button u_K1 (.out(K1));
  Button u_K2 (.out(K2));
  Multiplexer #(.select(2), .width(4), .enable("false")) multiplexer_1 (
    .in0(4'b0000), .in1(HEX1), .in2(HEX0), .in3(4'b0000), .out(multiplexer_1_out), .sel(uc_1_rgin));
  UC uc_1 (
    .CLK(S9), .dataBus_16(ROM_data), .CLR(S0), .X_forJMP(X_forJMP), .RgIN(uc_1_rgin), .X(X), .ULA(uc_1_ula),
    .RgTO(uc_1_rgto), .JMP_ULA(ENABLE_ULA), .JMP_RESET_REG(RESET_REG), .JMP_RESET_PC(RESET_PC), .JMP_X(JMP_X));  // open: NULL
  or or_2 (or_2_out, S0, RESET_REG);
  ULA4 ULA (.A(multiplexer_1_out), .B(X), .Op(uc_1_ula), .R(ULA_r));
  REG16 reg16_1 (.CLK(S9), .D(ROM_data), .CLR(S0), .Load(1'b1), .Q({HEX5, HEX4, HEX3, HEX2}));  // open: PR
  REG4 reg4_2 (.CLK(S9), .D(TO_REG2), .CLR(or_2_out), .Load(and_2_out), .Q(HEX0));  // open: PR
  and and_2 (and_2_out, ENABLE_ULA, LOAD_REG2);
  Demultiplexer #(.select(2), .width(4), .enable("false")) demultiplexer_1 (
    .out1(TO_REG1), .out2(TO_REG2), .in(ULA_r), .sel(uc_1_rgto));  // open: out0, out3
  // Digital_Oscilloscope digital_oscilloscope_1: pin names not known; wires that end beside it: S9, HEX1[0], HEX1[1], HEX1[2]
  // Digital_Oscilloscope digital_oscilloscope_2: pin names not known; wires that end beside it: HEX1[3], S9, HEX0[0], HEX0[1], HEX0[2], HEX0[3]
  Demultiplexer #(.select(2), .enable("false")) demultiplexer_2 (
    .out1(LOAD_REG1), .out2(LOAD_REG2), .in(1'b1), .sel(uc_1_rgto));  // open: out0, out3

  // Other names for the same wires on the sheet: Q_REG1[3:0] = HEX1; Q_REG2[3:0] = HEX0

  // Notes on the sheet:
  //   CLK
  //   MEMORY
  //   S0 = CLR, S9 = CLK
  //   Counter com JUMP
  //   REG1
  //   REG2
  //   CLR
  //   contents of ROM (hex, n*v repeats v):
  //   6004 9102 6201 6305 9002 6002 9003 400 c0d 4*0 9002 6302 6101 9302 6200 6003 800
  //   Escolhe o Reg que vai para ULA
  //   A = Q_RgIN
  //   B = X
  //   Escolhe o Reg no qual será guardado o resultado
  //   REG1
  //   REG2
endmodule

module REG4 (
  input  PR,
  input  CLR,
  input  Load,
  input  CLK,
  input  [3:0] D,
  output [3:0] Q
);

  wire multiplexer_1_out, multiplexer_2_out, multiplexer_3_out, multiplexer_4_out;

  Multiplexer #(.enable("false")) multiplexer_1 (.in0(Q[0]), .in1(D[0]), .out(multiplexer_1_out), .sel(Load));
  Multiplexer #(.enable("false")) multiplexer_2 (.in0(Q[1]), .in1(D[1]), .out(multiplexer_2_out), .sel(Load));
  Multiplexer #(.enable("false")) multiplexer_3 (.in0(Q[2]), .in1(D[2]), .out(multiplexer_3_out), .sel(Load));
  Multiplexer #(.enable("false")) multiplexer_4 (.in0(Q[3]), .in1(D[3]), .out(multiplexer_4_out), .sel(Load));
  D_Flip_Flop d_ff_1 (.clk(CLK), .D(multiplexer_1_out), .Q(Q[0]), .preset(PR), .reset(CLR));  // open: Qn
  D_Flip_Flop d_ff_2 (.clk(CLK), .D(multiplexer_2_out), .Q(Q[1]), .preset(PR), .reset(CLR));  // open: Qn
  D_Flip_Flop d_ff_3 (.clk(CLK), .D(multiplexer_3_out), .Q(Q[2]), .preset(PR), .reset(CLR));  // open: Qn
  D_Flip_Flop d_ff_4 (.clk(CLK), .D(multiplexer_4_out), .Q(Q[3]), .preset(PR), .reset(CLR));  // open: Qn

  // Other names for the same wires on the sheet: Q1 = Q[0]; Q2 = Q[1]; Q3 = Q[2]; Q4 = Q[3]

  // Notes on the sheet:
  //   Registrador Paralelo
endmodule

module REG16 (
  input  PR,
  input  CLR,
  input  Load,
  input  CLK,
  input  [15:0] D,
  output [15:0] Q
);

  REG4 reg4_1 (.CLK(CLK), .D(D[3:0]), .PR(PR), .CLR(CLR), .Load(Load), .Q(Q[3:0]));
  REG4 reg4_2 (.CLK(CLK), .D(D[7:4]), .PR(PR), .CLR(CLR), .Load(Load), .Q(Q[7:4]));
  REG4 reg4_3 (.CLK(CLK), .D(D[11:8]), .PR(PR), .CLR(CLR), .Load(Load), .Q(Q[11:8]));
  REG4 reg4_4 (.CLK(CLK), .D(D[15:12]), .PR(PR), .CLR(CLR), .Load(Load), .Q(Q[15:12]));

  // Notes on the sheet:
  //   Registrador Paralelo
endmodule

module ULA4 (
  input  [3:0] A,
  input  [3:0] B,
  input  [1:0] Op,
  output [3:0] R
);

  wire [3:0] adder_1_out, divider_1_out, multiplier_1_out, subtractor_1_out;

  Adder #(.width(4)) adder_1 (.a(A), .b(B), .out(adder_1_out));  // open: cin, cout
  Multiplier #(.width(4)) multiplier_1 (.a(B), .b(4'b0010), .out(multiplier_1_out));  // open: cin, cout
  Subtractor #(.width(4)) subtractor_1 (.a(A), .b(B), .out(subtractor_1_out));  // open: bin, bout
  Divider #(.width(4)) divider_1 (.a(B), .b(4'b0010), .out(divider_1_out));  // open: upper, rem
  Multiplexer #(.select(2), .width(4), .enable("false")) multiplexer_1 (
    .in0(adder_1_out), .in1(multiplier_1_out), .in2(subtractor_1_out), .in3(divider_1_out), .out(R), .sel(Op));

  // Notes on the sheet:
  //   A = REG_IN
  //   B = Operando
  //   REG_in + oper
  //   Operan * 2
  //   REG_in - oper
  //   Operan / 2
endmodule

module UC (
  input  CLK,
  input  [15:0] dataBus_16,
  input  CLR,
  output [1:0] RgIN,
  output [3:0] X,
  output [3:0] NULL,
  output [1:0] ULA,
  output [1:0] RgTO,
  output JMP_ULA,
  output JMP_RESET_REG,
  output [3:0] X_forJMP,
  output JMP_RESET_PC,
  output JMP_X
);

  wire and_1_out, and_2_out, and_3_out, and_4_out, demultiplexer_1_out1, demultiplexer_1_out2,
       demultiplexer_2_out3, not_1_out, not_2_out, not_3_out, not_4_out;
  wire [11:10] reg16_1_q;

  REG16 reg16_1 (
    .CLK(CLK), .D(dataBus_16), .CLR(and_1_out), .Load(1'b1), .Q({RgTO, RgIN, reg16_1_q, ULA, NULL, X}));  // open: PR
  and and_1 (and_1_out, CLR, not_1_out);
  not not_1 (not_1_out, CLK);
  Demultiplexer #(.select(2), .enable("false")) demultiplexer_1 (
    .out0(JMP_ULA), .out1(demultiplexer_1_out1), .out2(demultiplexer_1_out2), .in(1'b1), .sel(reg16_1_q));  // open: out3
  REG4 reg4_1 (.CLK(CLK), .D(dataBus_16[3:0]), .CLR(CLR), .Load(1'b1), .Q(X_forJMP));  // open: PR
  Demultiplexer #(.select(2), .enable("false")) demultiplexer_2 (
    .out3(demultiplexer_2_out3), .in(1'b1), .sel(dataBus_16[11:10]));  // open: out0, out1, out2
  and and_2 (and_2_out, not_2_out, JMP_X);
  not not_2 (not_2_out, CLK);
  D_Flip_Flop d_ff_1 (.clk(CLK), .D(demultiplexer_2_out3), .Q(JMP_X), .reset(and_2_out));  // open: Qn, preset
  D_Flip_Flop d_ff_2 (.clk(CLK), .D(demultiplexer_1_out1), .Q(JMP_RESET_REG), .reset(and_3_out));  // open: Qn, preset
  and and_3 (and_3_out, JMP_RESET_REG, not_3_out);
  not not_3 (not_3_out, CLK);
  and and_4 (and_4_out, JMP_RESET_PC, not_4_out);
  D_Flip_Flop d_ff_3 (.clk(CLK), .D(demultiplexer_1_out2), .Q(JMP_RESET_PC), .reset(and_4_out));  // open: Qn, preset
  not not_4 (not_4_out, CLK);

  // Notes on the sheet:
  //   -> Memoria vazia
  //   -> Operando, valor generico usado em operações da ULA e de JUMP
endmodule

module Count8 (
  input  JMP,
  input  [3:0] X,
  input  CLR,
  input  CLK,
  input  Vcc,
  output [7:0] Q
);

  wire and_6_out, or_1_out, or_2_out, or_3_out, or_4_out, T2, T3, T4, T5, T6;

  COUNTER8_JMP_UNIT counter8_jmp_unit_1 (.CLK(CLK), .T(Vcc), .X(X[0]), .CLR(CLR), .JMP(JMP), .Q(Q[0]));  // open: Q_NOT
  COUNTER8_JMP_UNIT counter8_jmp_unit_2 (.CLK(CLK), .T(Q[0]), .X(X[1]), .CLR(CLR), .JMP(JMP), .Q(Q[1]));  // open: Q_NOT
  and and_1 (T2, Q[0], Q[1]);
  COUNTER8_JMP_UNIT counter8_jmp_unit_3 (.CLK(CLK), .T(T2), .X(X[2]), .CLR(CLR), .JMP(JMP), .Q(Q[2]));  // open: Q_NOT
  and and_2 (T3, T2, Q[2]);
  COUNTER8_JMP_UNIT counter8_jmp_unit_4 (.CLK(CLK), .T(T3), .X(X[3]), .CLR(CLR), .JMP(JMP), .Q(Q[3]));  // open: Q_NOT
  and and_3 (T4, T3, Q[3]);
  or or_1 (or_1_out, CLR, JMP);
  Hex_Digit_Display hex_digit_display_1 (.value(Q[7:4]));  // open: dp
  Hex_Digit_Display hex_digit_display_2 (.value(Q[3:0]));  // open: dp
  T_Flip_Flop t_ff_1 (.clk(CLK), .T(T4), .Q(Q[4]), .reset(or_1_out));  // open: Qn, preset
  and and_4 (T5, T4, Q[4]);
  T_Flip_Flop t_ff_2 (.clk(CLK), .T(T5), .Q(Q[5]), .reset(or_2_out));  // open: Qn, preset
  or or_2 (or_2_out, CLR, JMP);
  and and_5 (T6, T5, Q[5]);
  T_Flip_Flop t_ff_3 (.clk(CLK), .T(T6), .Q(Q[6]), .reset(or_3_out));  // open: Qn, preset
  or or_3 (or_3_out, CLR, JMP);
  and and_6 (and_6_out, T6, Q[6]);
  T_Flip_Flop t_ff_4 (.clk(CLK), .T(and_6_out), .Q(Q[7]), .reset(or_4_out));  // open: Qn, preset
  or or_4 (or_4_out, CLR, JMP);

  // Notes on the sheet:
  //   Contador de 8 Bits Síncrono com JUMP
endmodule

module COUNTER8_JMP_UNIT (
  input  X,
  input  CLK,
  input  T,
  input  CLR,
  input  JMP,
  output Q,
  output Q_NOT
);

  wire and_1_out, and_2_out, not_1_out, or_1_out;

  and and_1 (and_1_out, X, JMP);
  T_Flip_Flop t_ff_1 (.clk(CLK), .T(T), .Q(Q), .Qn(Q_NOT), .preset(and_1_out), .reset(or_1_out));
  or or_1 (or_1_out, CLR, and_2_out);
  and and_2 (and_2_out, not_1_out, JMP);
  not not_1 (not_1_out, X);
endmodule

module ROM_256x16 (
  input  [7:0] Address,
  input  CLK,
  output [15:0] Mem
);

  wire [15:0] ROM_data;

  ROM #(.dataWidth(16), .Select("low")) ROM (.addr(Address), .data(ROM_data));
  REG16 REG16 (.CLK(CLK), .D(ROM_data), .Load(1'b1), .Q(Mem));  // open: PR, CLR

  // Notes on the sheet:
  //   contents of ROM (hex, n*v repeats v):
  //   4103 9202 6001 4307 0 c0c 13*0 800
endmodule
